# Fritzing sketch AM2320_wbgt_for_breadboard (saved by Fritzing 0.9.4)
breadboards: 1

parts:
  Mod1 = Raspberry Pi 4B
  AM1 = AM2320 Humidity and Temperature Sensor [part_number="Adafruit #3721"]

nets:
  3V3: Mod1.3V3, AM1.VDD
  N1: Mod1.GPIO2, AM1.SDA
  N2: Mod1.GPIO3, AM1.SCL
  GND: Mod1.GND, AM1.GND

custom parts:
  AM2320 Humidity and Temperature Sensor: AM2320 I2C Humidity and Temperature Sensor
